// Digital circuit flipfloprepresentation.dig as structural Verilog
module flipfloprepresentation (
  input  A,
  input  B,
  input  C,
  output Q_1,
  output Q_0
);

  wire and_1_out, and_2_out, and_3_out, and_4_out, not_1_out, not_2_out, not_3_out, or_1_out, or_2_out;

  not not_1 (not_1_out, B);
  not not_2 (not_2_out, Q_1);
  not not_3 (not_3_out, Q_0);
  and and_1 (and_1_out, B, Q_0, not_2_out);
  and and_2 (and_2_out, not_3_out, Q_1);
  and and_3 (and_3_out, A, not_3_out, not_2_out);
  and and_4 (and_4_out, not_1_out, Q_0, not_2_out);
  or or_1 (or_1_out, and_1_out, and_2_out);
  or or_2 (or_2_out, and_3_out, and_4_out);
  D_FF Q_1_n (.D(or_1_out), .C(C), .Q(Q_1));  // open: nQ
  D_FF Q_0_n (.D(or_2_out), .C(C), .Q(Q_0));  // open: nQ

  // Other names for the same wires on the sheet: Q_0_n = Q_0; Q_1_n = Q_1

  // Notes on the sheet:
  //   C: Hz: 2
endmodule
